# Fritzing sketch anti_wallet_lost (saved by Fritzing 0.9.3b)
breadboards: 1

parts:
  IC1 = 433Mhz Superheterodyne RF Receiver
  IC2 = Set 433Mhz Superheterodyne RF Transmitter 3.3V
  U1 = BATTERY-2 [package=battery-aaa]
  U2 = BATTERY-2 [package=battery-aaa]
  U3 = BATTERY-2 [package=battery-aaa]
  U4 = BATTERY-2 [package=battery-aaa]
  U5 = BATTERY-2 [package=battery-aaa]
  U6 = BATTERY-2 [package=battery-aaa]
  Part1 = Arduino Pro Mini (5V)
  Part2 = Arduino Pro Mini (5V)
  Passive_Buzzer_80dB_2700Hz1 = 3.3V Integrated Electromagnetic Passive Buzzer 80dB 2700Hz

nets:
  N1: IC1.VCC_pin, U1.-1, U2.-1, U3.+1, Part1.VCC
  N2: IC1.DO_pin, Part1.D8
  N3: IC1.GND_pin, U1.+1, U2.+1, U3.-1, Part1.GND, Passive_Buzzer_80dB_2700Hz1.Pin_GND
  N4: IC2.DAT_PIN, Part2.D8
  N5: IC2.VCC_PIN, U4.+1, U5.+1, U6.-1
  N6: IC2.GND_PIN, U4.-1, U5.-1, U6.+1
  N7: Part1.D3, Passive_Buzzer_80dB_2700Hz1.Pin_Signal

custom parts:
  433Mhz Superheterodyne RF Receiver: Receiver Module: Features: RX470-4 superheterodyne wireless receiver module is receiving UHF ASK demodulators supporting ASK and OOK modulation. The receiver module has high sensitivity (-108dBm). Low-power performance, along with high dynamic range (greater than 60dB). Module uses highly integrated chip, built front-end low-noise amplifier, mixers, filters, frequency synthesizer circuit,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
  Set 433Mhz Superheterodyne RF Transmitter 3.3V: Transmitter Module: Features: WL102-341 transmitter module is UHF ASK modulated transmitters, support ASK and OOK modulation. The transmitter module integrates an analog PLL circuit and ASK modulation circuit, with a high level of integration, etc., can be applied with a short-range wireless communications. Operating frequency 433MHz, transmit power is greater than 11dBm. Transmitter Module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
  3.3V Integrated Electromagnetic Passive Buzzer 80dB 2700Hz: Passive Buzzer 80dB 2700Hz No. Item Unit Specification Condition 1 Oscillation Frequency Hz 2700 Vo-p=1/2duty, square wave 2 Operating Voltage Vo-p 2~4 3 Rated Voltage Vo-p 3 4 Current Consumption mA Max.100 at Rated Voltage 5 Sound Pressure Level dB MIN.80 at 10cm at Rated Voltage 6 Coil Resistance Ω 16±3 7 Operating Temperature ℃ -20~+60 8 Storage Temperature ℃ -30~+70 9 Dimensions mm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
